# Fritzing sketch battery-power-layout (saved by Fritzing 0.9.4)

parts:
  KT1 = SriKIT Simple Clock Module [part_number=KT0001 package=THT]
  VCC1 = Battery

nets:
  N1: KT1.BAT-, VCC1.-
  N2: KT1.BAT+, VCC1.+

notes:
  2 x 1.5V AA Batteries

custom parts:
  SriKIT Simple Clock Module: Simple clock module
