# Fritzing sketch buzzer-alarm-layout (saved by Fritzing 0.9.4)

parts:
  KT1 = SriKIT Simple Clock Module [part_number=KT0001 package=THT]
  J1 = Piezo Speaker

nets:
  N1: KT1.OUT+, J1.pin1

notes:
  +
  -
  Input from +5V Power Supply
  Active 5V buzzer

custom parts:
  SriKIT Simple Clock Module: Simple clock module
